# Fritzing sketch wiring (saved by Fritzing 0.9.3b)
breadboards: 1

parts:
  DHT1 = DHT22 Humidity and Temperature Sensor
  Part1 = Logic Level Converter
  Part2 = Adafruit SGP30 Gas Sensor
  Part3 = Adafruit T-Cobbler Plus [part_number="Adafruit #1989 and #2028"]

nets:
  VDD: DHT1.VDD, Part1.HV, Part3.+5V
  N1: DHT1.DATA, Part1.TX2_HV
  GND: DHT1.NULL, Part1.GND, Part2.GND, Part3.GND
  N2: Part1.TX2_LV, Part3.GPIO4
  VIN: Part1.LV, Part2.VIN, Part3.+3.3V
  N3: Part2.SCL, Part3.SCL
  N4: Part2.SDA, Part3.SDA

notes:
  TTL (5V => 3.3V logic level shifter)
  DHT22 temp/hum sensor
  SGP30 CO2 sensor

custom parts:
  Adafruit T-Cobbler Plus: The Raspberry Pi has landed on the Maker World like a 40-GPIO pinned, quad-USB ported, credit card sized bomb of DIY joy. And while you can use most of our great Model B accessories by hooking up our downgrade cable, its probably a good time to upgrade your set up and accessorize using all of the 40 pins. That's why we now carry the Assembled Adafruit Pi T-Cobbler Plus - Breakout + Cable for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
